// Digital circuit ALU.dig as structural Verilog
module ALU (
  input  [1:0] Sel,
  input  Cin,
  input  [15:0] A,
  input  [15:0] B,
  output Z,
  output N,
  output S3,
  output S2,
  output S1,
  output S0,
  output S4,
  output S7,
  output S6,
  output S5,
  output S8,
  output S11,
  output S10,
  output S9,
  output S12,
  output S13,
  output S14,
  output S15,
  output C_out
);

  wire decoder_1_out_1, extended_adder_1_cout, extended_adder_2_cout, extended_adder_3_cout,
       extended_adder_4_cout, extended_adder_5_cout, extended_adder_6_cout, extended_adder_7_cout,
       extended_adder_8_cout, extended_adder_9_cout, extended_adder_10_cout, extended_adder_11_cout,
       extended_adder_12_cout, extended_adder_13_cout, extended_adder_14_cout, extended_adder_15_cout,
       or_1_out;
  wire [1:0] decoder_1_out_3;

  Decoder #(.Selector_Bits(2)) decoder_1 (
    .sel(Sel), .out_1(decoder_1_out_1), .out_2(decoder_1_out_3[0]), .out_3(decoder_1_out_3[1]));  // open: out_0
  or or_1 (or_1_out, Cin, decoder_1_out_1);
  extended_adder extended_adder_1 (
    .Cin(or_1_out), .A(A[0]), .B(B[0]), .Opt(decoder_1_out_3), .Sub(decoder_1_out_1),
    .Cout(extended_adder_1_cout), .S(S0));
  extended_adder extended_adder_2 (
    .Cin(extended_adder_1_cout), .A(A[1]), .B(B[1]), .Opt(decoder_1_out_3), .Sub(decoder_1_out_1),
    .Cout(extended_adder_2_cout), .S(S1));
  extended_adder extended_adder_3 (
    .Cin(extended_adder_2_cout), .A(A[2]), .B(B[2]), .Opt(decoder_1_out_3), .Sub(decoder_1_out_1),
    .Cout(extended_adder_3_cout), .S(S2));
  extended_adder extended_adder_4 (
    .Cin(extended_adder_3_cout), .A(A[3]), .B(B[3]), .Opt(decoder_1_out_3), .Sub(decoder_1_out_1),
    .Cout(extended_adder_4_cout), .S(S3));
  extended_adder extended_adder_5 (
    .Cin(extended_adder_4_cout), .A(A[4]), .B(B[4]), .Opt(decoder_1_out_3), .Sub(decoder_1_out_1),
    .Cout(extended_adder_5_cout), .S(S4));
  extended_adder extended_adder_6 (
    .Cin(extended_adder_5_cout), .A(A[5]), .B(B[5]), .Opt(decoder_1_out_3), .Sub(decoder_1_out_1),
    .Cout(extended_adder_6_cout), .S(S5));
  extended_adder extended_adder_7 (
    .Cin(extended_adder_6_cout), .A(A[6]), .B(B[6]), .Opt(decoder_1_out_3), .Sub(decoder_1_out_1),
    .Cout(extended_adder_7_cout), .S(S6));
  extended_adder extended_adder_8 (
    .Cin(extended_adder_7_cout), .A(A[7]), .B(B[7]), .Opt(decoder_1_out_3), .Sub(decoder_1_out_1),
    .Cout(extended_adder_8_cout), .S(S7));
  extended_adder extended_adder_9 (
    .Cin(extended_adder_8_cout), .A(A[8]), .B(B[8]), .Opt(decoder_1_out_3), .Sub(decoder_1_out_1),
    .Cout(extended_adder_9_cout), .S(S8));
  extended_adder extended_adder_10 (
    .Cin(extended_adder_9_cout), .A(A[9]), .B(B[9]), .Opt(decoder_1_out_3), .Sub(decoder_1_out_1),
    .Cout(extended_adder_10_cout), .S(S8));
  extended_adder extended_adder_11 (
    .Cin(extended_adder_10_cout), .A(A[10]), .B(B[10]), .Opt(decoder_1_out_3), .Sub(decoder_1_out_1),
    .Cout(extended_adder_11_cout), .S(S8));
  extended_adder extended_adder_12 (
    .Cin(extended_adder_11_cout), .A(A[11]), .B(B[11]), .Opt(decoder_1_out_3), .Sub(decoder_1_out_1),
    .Cout(extended_adder_12_cout), .S(S11));
  extended_adder extended_adder_13 (
    .Cin(extended_adder_12_cout), .A(A[12]), .B(B[12]), .Opt(decoder_1_out_3), .Sub(decoder_1_out_1),
    .Cout(extended_adder_13_cout), .S(S12));
  extended_adder extended_adder_14 (
    .Cin(extended_adder_13_cout), .A(A[13]), .B(B[13]), .Opt(decoder_1_out_3), .Sub(decoder_1_out_1),
    .Cout(extended_adder_14_cout), .S(S13));
  extended_adder extended_adder_15 (
    .Cin(extended_adder_14_cout), .A(A[14]), .B(B[14]), .Opt(decoder_1_out_3), .Sub(decoder_1_out_1),
    .Cout(extended_adder_15_cout), .S(S14));
  extended_adder extended_adder_16 (
    .Cin(extended_adder_15_cout), .A(A[15]), .B(B[15]), .Opt(decoder_1_out_3), .Sub(decoder_1_out_1),
    .Cout(C_out), .S(S15));
  nor nor_1 (Z, S0, S1, S2, S3, S4, S5, S6, S7, S8, S8, S8, S11, S12, S13, S14, S15);
  // NOr nor_2 is placed but not wired
  // Pins of 4 and 16 bits meet at A
  // Pins of 4 and 16 bits meet at B

  assign S9 = S8;
  assign S10 = S8;
endmodule
