// Digital circuit ALU_Streamlined.dig as structural Verilog
module ALU_Streamlined (
  input  [15:0] A,
  input  [15:0] B,
  input  [2:0] Sel,
  input  C_in,
  input  Inv_A,
  input  Inv_b,
  output [15:0] Out,
  output C_out
);

  wire add_1_c_o, sub_1_c_o;
  wire [15:0] add_1_s, and_1_out, div_1_q, mul_1_mul, mul_1_mul_2, multiplexer_1_out, multiplexer_2_out,
       not_1_out, not_2_out, or_1_out, sub_1_s, xor_1_out;

  assign not_1_out = ~A;  // Not not_1, 16 bits wide
  assign not_2_out = ~B;  // Not not_2, 16 bits wide
  Multiplexer #(.Bits(16)) multiplexer_1 (.sel(Inv_A), .in_0(A), .in_1(not_1_out), .out(multiplexer_1_out));
  Multiplexer #(.Bits(16)) multiplexer_2 (.sel(Inv_b), .in_0(B), .in_1(not_2_out), .out(multiplexer_2_out));
  Add #(.Bits(16)) add_1 (.a(multiplexer_1_out), .b(multiplexer_2_out), .c_i(C_in), .s(add_1_s), .c_o(add_1_c_o));
  Sub #(.Bits(16)) sub_1 (.a(multiplexer_1_out), .b(multiplexer_2_out), .c_i(C_in), .s(sub_1_s), .c_o(sub_1_c_o));
  Mul #(.Bits(16)) mul_1 (.a(multiplexer_1_out), .b(multiplexer_2_out), .mul({mul_1_mul_2, mul_1_mul}));
  Div #(.Bits(16)) div_1 (.a(multiplexer_1_out), .b(multiplexer_2_out), .q(div_1_q));  // open: r
  assign and_1_out = multiplexer_1_out & multiplexer_2_out;  // And and_1, 16 bits wide
  assign or_1_out = multiplexer_1_out | multiplexer_2_out;  // Or or_1, 16 bits wide
  assign xor_1_out = multiplexer_1_out ^ multiplexer_2_out;  // XOr xor_1, 16 bits wide
  Multiplexer multiplexer_3 (.sel(Sel[0]), .in_0(add_1_c_o), .in_1(sub_1_c_o), .out(C_out));
  Multiplexer #(.Bits(16), .Selector_Bits(3)) multiplexer_4 (
    .sel(Sel), .in_0(add_1_s), .in_1(sub_1_s), .in_2(mul_1_mul), .in_3(mul_1_mul_2), .in_4(div_1_q),
    .in_5(and_1_out), .in_6(or_1_out), .in_7(xor_1_out), .out(Out));
endmodule
