// Digital circuit reg_file.dig as structural Verilog
module reg_file (
  input  [2:0] RS1,
  input  [2:0] RS2,
  input  [2:0] WS,
  input  WE,
  input  [15:0] IN,
  input  clk,
  input  [15:0] FL_IN,
  input  FL_EN,
  output [15:0] OUT1,
  output [15:0] OUT2
);

  wire demultiplexer_1_out_0, demultiplexer_1_out_1, demultiplexer_1_out_2, demultiplexer_1_out_3,
       demultiplexer_1_out_4, demultiplexer_1_out_5, or_1_out;
  wire [15:0] FL_q, R1_q, R2_q, R3_q, R4_q, RZ_q;

  Demultiplexer #(.Selector_Bits(3)) demultiplexer_1 (
    .sel(WS), .in(WE), .out_0(demultiplexer_1_out_0), .out_1(demultiplexer_1_out_1),
    .out_2(demultiplexer_1_out_2), .out_3(demultiplexer_1_out_3), .out_4(demultiplexer_1_out_4),
    .out_5(demultiplexer_1_out_5));  // open: out_6, out_7
  or or_1 (or_1_out, demultiplexer_1_out_5, FL_EN);
  Register #(.Bits(16)) RZ (.D({16{1'b0}}), .C(clk), .en(demultiplexer_1_out_0), .Q(RZ_q));
  Register #(.Bits(16)) R1 (.D(IN), .C(clk), .en(demultiplexer_1_out_1), .Q(R1_q));
  Register #(.Bits(16)) R2 (.D(IN), .C(clk), .en(demultiplexer_1_out_2), .Q(R2_q));
  Register #(.Bits(16)) R3 (.D(IN), .C(clk), .en(demultiplexer_1_out_3), .Q(R3_q));
  Register #(.Bits(16)) R4 (.D(IN), .C(clk), .en(demultiplexer_1_out_4), .Q(R4_q));
  Register #(.Bits(16)) FL (.D(FL_IN), .C(clk), .en(or_1_out), .Q(FL_q));
  Multiplexer #(.Selector_Bits(3), .Bits(16)) multiplexer_1 (
    .sel(RS1), .in_0(RZ_q), .in_1(R1_q), .in_2(R2_q), .in_3(R3_q), .in_4(R4_q), .in_5(FL_q),
    .in_6({16{1'b0}}), .in_7({16{1'b0}}), .out(OUT1));
  Multiplexer #(.Selector_Bits(3), .Bits(16)) multiplexer_2 (
    .sel(RS2), .in_0(RZ_q), .in_1(R1_q), .in_2(R2_q), .in_3(R3_q), .in_4(R4_q), .in_5(FL_q),
    .in_6({16{1'b0}}), .in_7({16{1'b0}}), .out(OUT2));

  // Notes on the sheet:
  //   RS1: The index of the register which should output its value to OUT1.
  //   RS2: The index of the register which should output its value to OUT2.
  //   WS: The index of the register which should save the value on IN on the next clock cycle (if WE is high).
  //   WE: Whether the register selected by WS should save the value from IN on the next cycle.
  //   IN: The value to be saved into the register specified by WS if WE is high,
  //   OUT1: The value in the register specified by RS1.
  //   OUT2: The value in the register specified by RS2.
  //   FL_IN: The value to be saved into the register specified by WS if WE is high,
  //   FL_EN: Whether the register selected by WS should save the value from IN on the next cycle.
endmodule

/* Test case:
clk RS1 RS2 WS WE IN OUT1 OUT2
c 0 0 0 1 0x1234 0x0000 0x0000
c 1 1 1 1 0x1234 0x1234 0x1234
c 2 1 2 1 0xBEEF 0xBEEF 0x1234
c 3 2 3 1 0xDEAD 0xDEAD 0xBEEF
c 4 3 4 1 0xFFFF 0xFFFF 0xDEAD
c 4 3 4 0 0xABCD 0xFFFF 0xDEAD
c 4 3 3 0 0xABCD 0xFFFF 0xDEAD
c 2 1 2 0 0xABCD 0xBEEF 0x1234
c 2 1 1 0 0xABCD 0xBEEF 0x1234
c 2 1 3 1 0xBADE 0xBEEF 0x1234
c 1 3 3 1 0xBADE 0x1234 0xBADE
c 1 1 3 0 0x1234 0x1234 0x1234
c 3 4 1 1 0x0000 0xBADE 0xFFFF
c 1 1 3 0 0x1234 0x0000 0x0000
c 3 4 0 1 0xBADE 0xBADE 0xFFFF
c 0 0 3 1 0xBADE 0x0000 0x0000
*/
