// Digital circuit cpu.dig as structural Verilog
module cpu (
  input  CLK
);

  wire and_1_out, and_2_out, and_3_out, and_4_out, condition_unit_1_condexe, control_unit_1_alusrcd,
       control_unit_1_branchd, control_unit_1_flagen, control_unit_1_flagwrited, control_unit_1_insertnop,
       control_unit_1_ldr, control_unit_1_memtoregd, control_unit_1_memwrited, control_unit_1_pcsrcd,
       control_unit_1_regwrited, control_unit_1_sethd, ex_mem_ppr_1_p11, ex_mem_ppr_1_p12, ex_mem_ppr_1_p13,
       ex_mem_ppr_1_p14, ex_mem_ppr_1_p15, ex_mem_ppr_1_p19, hazard_unit_1_flushd, hazard_unit_1_flushe,
       hazard_unit_1_stalld, hazard_unit_1_stallf, id_ex_ppr_1_alusrce, id_ex_ppr_1_branche,
       id_ex_ppr_1_conde, id_ex_ppr_1_flagwritee, id_ex_ppr_1_ldre, id_ex_ppr_1_memtorege,
       id_ex_ppr_1_memwritee, id_ex_ppr_1_pcsrce, id_ex_ppr_1_regwritee, id_ex_ppr_1_sethe,
       mem_wb_ppr_1_memtoregw, mem_wb_ppr_1_pcsrcw, mem_wb_ppr_1_regwritew, mem_wb_ppr_1_sethw, not_1_out,
       not_2_out;
  wire [1:0] control_unit_1_aluctrld, hazard_unit_1_forwardae, hazard_unit_1_forwardbe, id_ex_ppr_1_aluctrle;
  wire [2:0] ex_mem_ppr_1_p18, id_ex_ppr_1_wae, mem_wb_ppr_1_wa3w;
  wire [3:0] alu_1_flag, condition_unit_1_flagsm, id_ex_ppr_1_flagse, PC_q;
  wire [15:0] alu_1_result, bitextender_1_out, bitextender_2_out, ex_mem_ppr_1_p16, ex_mem_ppr_1_p17,
       id_ex_ppr_1_ra1e, id_ex_ppr_1_ra2e, id_ex_ppr_1_rd1e, id_ex_ppr_1_rd2e, id_ex_ppr_1_sei16e,
       if_id_ppr_1_insn_out, mem_wb_ppr_1_aluresultw, mem_wb_ppr_1_readdataw, multiplexer_1_out,
       multiplexer_2_out, multiplexer_3_out, multiplexer_4_out, multiplexer_5_out, multiplexer_6_out,
       multiplexer_7_out, plus_1_s, RAM_d1, RAM_d2, reg_address_extender_1_out, reg_address_extender_2_out,
       reg_address_extender_3_out, reg_address_extender_4_out, reg_address_extender_5_out, reg_file_1_out1,
       reg_file_1_out2;
  wire [15:4] PC_q_2;

  Seven_Seg_Hex seven_seg_hex_1 (.d(PC_q_2[11:8]), .dp(1'b0));
  Seven_Seg_Hex seven_seg_hex_2 (.d(PC_q_2[15:12]), .dp(1'b0));
  Seven_Seg_Hex seven_seg_hex_3 (.d(PC_q), .dp(1'b0));
  Seven_Seg_Hex seven_seg_hex_4 (.d(PC_q_2[7:4]), .dp(1'b0));
  not not_1 (not_1_out, hazard_unit_1_stallf);
  Multiplexer #(.Bits(16)) multiplexer_1 (
    .sel(and_4_out), .in_0(multiplexer_2_out), .in_1(alu_1_result), .out(multiplexer_1_out));
  Multiplexer #(.Bits(16)) multiplexer_2 (
    .sel(mem_wb_ppr_1_pcsrcw), .in_0(plus_1_s), .in_1(multiplexer_7_out), .out(multiplexer_2_out));
  Register #(.Bits(16), .isProgramCounter("true")) PC (
    .D(multiplexer_1_out), .C(CLK), .en(not_1_out), .Q({PC_q_2, PC_q}));
  Add #(.Bits(16)) plus_1 (.a(16'h1), .b({PC_q_2, PC_q}), .c_i(1'b0), .s(plus_1_s));  // open: c_o
  RAMDualAccess #(.AddrBits(16), .isProgramMemory("true"), .Bits(16)) RAM (
    .str(ex_mem_ppr_1_p14), .C(CLK), .ld(ex_mem_ppr_1_p19), .A1(ex_mem_ppr_1_p16), .Din1(ex_mem_ppr_1_p17),
    .A2({PC_q_2, PC_q}), .D1(RAM_d1), .D2(RAM_d2));
  if_id_ppr if_id_ppr_1 (
    .CLK(CLK), .INSN_IN(RAM_d2), .INSN_OUT(if_id_ppr_1_insn_out), .CLR(hazard_unit_1_flushd), .EN(not_2_out));
  not not_2 (not_2_out, hazard_unit_1_stalld);
  control_unit control_unit_1 (
    .INST(if_id_ppr_1_insn_out), .PCSrcD(control_unit_1_pcsrcd), .RegWriteD(control_unit_1_regwrited),
    .MemToRegD(control_unit_1_memtoregd), .MemWriteD(control_unit_1_memwrited),
    .ALUCtrlD(control_unit_1_aluctrld), .BranchD(control_unit_1_branchd), .ALUSrcD(control_unit_1_alusrcd),
    .FlagWriteD(control_unit_1_flagwrited), .SethD(control_unit_1_sethd), .FlagEN(control_unit_1_flagen),
    .LDR(control_unit_1_ldr), .InsertNOP(control_unit_1_insertnop));
  Multiplexer #(.Bits(16)) multiplexer_3 (
    .sel(control_unit_1_insertnop), .in_0(if_id_ppr_1_insn_out), .in_1({16{1'b0}}), .out(multiplexer_3_out));
  BitExtender #(.inputBits(4)) bitextender_1 (.in(condition_unit_1_flagsm), .out(bitextender_1_out));
  reg_address_extender reg_address_extender_1 (.IN(multiplexer_3_out[2:0]), .OUT(reg_address_extender_1_out));
  reg_address_extender reg_address_extender_2 (.IN(multiplexer_3_out[6:4]), .OUT(reg_address_extender_2_out));
  reg_file reg_file_1 (
    .RS1(multiplexer_3_out[6:4]), .RS2(multiplexer_3_out[2:0]), .WS(mem_wb_ppr_1_wa3w),
    .WE(mem_wb_ppr_1_regwritew), .IN(multiplexer_7_out), .CLK(CLK), .FL_IN(bitextender_1_out),
    .FL_EN(control_unit_1_flagen), .PC_IN(multiplexer_1_out), .HE(mem_wb_ppr_1_sethw),
    .OUT1(reg_file_1_out1), .OUT2(reg_file_1_out2));
  BitExtender bitextender_2 (.in(multiplexer_3_out[7:0]), .out(bitextender_2_out));
  id_ex_ppr id_ex_ppr_1 (
    .CLK(CLK), .PCSrcD(control_unit_1_pcsrcd), .RegWriteD(control_unit_1_regwrited),
    .MemToRegD(control_unit_1_memtoregd), .MemWriteD(control_unit_1_memwrited),
    .ALUCtrlD(control_unit_1_aluctrld), .BranchD(control_unit_1_branchd), .ALUSrcD(control_unit_1_alusrcd),
    .FlagWriteD(control_unit_1_flagwrited), .SethD(control_unit_1_sethd), .LDRD(control_unit_1_ldr),
    .CondD(multiplexer_3_out[11]), .FlagsD(condition_unit_1_flagsm), .WAD(multiplexer_3_out[10:8]),
    .SEI16D(bitextender_2_out), .Ra1D(reg_address_extender_2_out), .Ra2D(reg_address_extender_1_out),
    .Rd1D(reg_file_1_out1), .Rd2D(reg_file_1_out2), .PCSrcE(id_ex_ppr_1_pcsrce),
    .RegWriteE(id_ex_ppr_1_regwritee), .MemToRegE(id_ex_ppr_1_memtorege), .MemWriteE(id_ex_ppr_1_memwritee),
    .ALUCtrlE(id_ex_ppr_1_aluctrle), .BranchE(id_ex_ppr_1_branche), .ALUSrcE(id_ex_ppr_1_alusrce),
    .FlagWriteE(id_ex_ppr_1_flagwritee), .SethE(id_ex_ppr_1_sethe), .LDRE(id_ex_ppr_1_ldre),
    .CondE(id_ex_ppr_1_conde), .FlagsE(id_ex_ppr_1_flagse), .WAE(id_ex_ppr_1_wae),
    .SEI16E(id_ex_ppr_1_sei16e), .Ra1E(id_ex_ppr_1_ra1e), .Ra2E(id_ex_ppr_1_ra2e), .Rd1E(id_ex_ppr_1_rd1e),
    .Rd2E(id_ex_ppr_1_rd2e), .CLR(hazard_unit_1_flushe));
  Multiplexer #(.Selector_Bits(2), .Bits(16)) multiplexer_4 (
    .sel(hazard_unit_1_forwardbe), .in_0(id_ex_ppr_1_rd2e), .in_1(multiplexer_7_out),
    .in_2(ex_mem_ppr_1_p16), .in_3({16{1'b0}}), .out(multiplexer_4_out));
  Multiplexer #(.Selector_Bits(2), .Bits(16)) multiplexer_5 (
    .sel(hazard_unit_1_forwardae), .in_0(id_ex_ppr_1_rd1e), .in_1(multiplexer_7_out),
    .in_2(ex_mem_ppr_1_p16), .in_3({16{1'b0}}), .out(multiplexer_5_out));
  hazard_unit hazard_unit_1 (
    .ALUSrcE(id_ex_ppr_1_alusrce), .RegWriteW(mem_wb_ppr_1_regwritew), .RegWriteM(ex_mem_ppr_1_p12),
    .RA1E(id_ex_ppr_1_ra1e), .WA3M(reg_address_extender_3_out), .RA2E(id_ex_ppr_1_ra2e),
    .WA3W(reg_address_extender_4_out), .MemtoRegE(id_ex_ppr_1_memtorege), .WA3E(reg_address_extender_5_out),
    .RA2D(reg_address_extender_1_out), .RA1D(reg_address_extender_2_out), .PCSrcD(control_unit_1_pcsrcd),
    .PCSrcE(id_ex_ppr_1_pcsrce), .PCSrcM(ex_mem_ppr_1_p11), .PCSrcW(mem_wb_ppr_1_pcsrcw),
    .BranchTakenE(and_4_out), .ForwardAE(hazard_unit_1_forwardae), .ForwardBE(hazard_unit_1_forwardbe),
    .StallD(hazard_unit_1_stalld), .StallF(hazard_unit_1_stallf), .FlushE(hazard_unit_1_flushe),
    .FlushD(hazard_unit_1_flushd));
  Multiplexer #(.Bits(16)) multiplexer_6 (
    .sel(id_ex_ppr_1_alusrce), .in_0(multiplexer_4_out), .in_1(id_ex_ppr_1_sei16e), .out(multiplexer_6_out));
  alu alu_1 (
    .A(multiplexer_5_out), .B(multiplexer_6_out), .ALUOP(id_ex_ppr_1_aluctrle), .RESULT(alu_1_result),
    .FLAG(alu_1_flag));
  condition_unit condition_unit_1 (
    .FlagWriteE(id_ex_ppr_1_flagwritee), .CondE(id_ex_ppr_1_conde), .FlagsE(id_ex_ppr_1_flagse),
    .ALUFlags(alu_1_flag), .FlagsM(condition_unit_1_flagsm), .CondExE(condition_unit_1_condexe));
  reg_address_extender reg_address_extender_3 (.IN(ex_mem_ppr_1_p18), .OUT(reg_address_extender_3_out));
  reg_address_extender reg_address_extender_4 (.IN(mem_wb_ppr_1_wa3w), .OUT(reg_address_extender_4_out));
  reg_address_extender reg_address_extender_5 (.IN(id_ex_ppr_1_wae), .OUT(reg_address_extender_5_out));
  and and_1 (and_1_out, id_ex_ppr_1_pcsrce, condition_unit_1_condexe);
  and and_2 (and_2_out, id_ex_ppr_1_regwritee, condition_unit_1_condexe);
  and and_3 (and_3_out, id_ex_ppr_1_memwritee, condition_unit_1_condexe);
  and and_4 (and_4_out, id_ex_ppr_1_branche, condition_unit_1_condexe);
  // ex_mem_ppr ex_mem_ppr_1: pin names not known; wires that end beside it: CLK, and_1_out, and_2_out, id_ex_ppr_1_memtorege, and_3_out, id_ex_ppr_1_sethe, alu_1_result, multiplexer_4_out, id_ex_ppr_1_wae, id_ex_ppr_1_ldre, ex_mem_ppr_1_p11, ex_mem_ppr_1_p12, ex_mem_ppr_1_p13, ex_mem_ppr_1_p14, ex_mem_ppr_1_p15, ex_mem_ppr_1_p16, ex_mem_ppr_1_p17, ex_mem_ppr_1_p18, ex_mem_ppr_1_p19
  mem_wb_ppr mem_wb_ppr_1 (
    .CLK(CLK), .PCSrcM(ex_mem_ppr_1_p11), .RegWriteM(ex_mem_ppr_1_p12), .MemToRegM(ex_mem_ppr_1_p13),
    .ReadDataM(RAM_d1), .SethM(ex_mem_ppr_1_p15), .ALUResultM(ex_mem_ppr_1_p16), .WA3M(ex_mem_ppr_1_p18),
    .PCSrcW(mem_wb_ppr_1_pcsrcw), .RegWriteW(mem_wb_ppr_1_regwritew), .MemToRegW(mem_wb_ppr_1_memtoregw),
    .ReadDataW(mem_wb_ppr_1_readdataw), .SethW(mem_wb_ppr_1_sethw), .ALUResultW(mem_wb_ppr_1_aluresultw),
    .WA3W(mem_wb_ppr_1_wa3w));
  Multiplexer #(.Bits(16)) multiplexer_7 (
    .sel(mem_wb_ppr_1_memtoregw), .in_0(mem_wb_ppr_1_aluresultw), .in_1(mem_wb_ppr_1_readdataw),
    .out(multiplexer_7_out));
endmodule
