// Digital circuit issue_queue.dig as structural Verilog
module issue_queue (
  input  CLK,
  input  [15:0] INSN,
  input  [15:0] TagDst
);

  wire comparator_1_eq, demultiplexer_1_out_0, demultiplexer_1_out_1, demultiplexer_1_out_2,
       demultiplexer_4_out_0, demultiplexer_4_out_1, demultiplexer_4_out_2, Is_I_Format_eq, not_1_out;
  wire [1:0] counter_1_out;
  wire [5:0] demultiplexer_2_out_0, demultiplexer_2_out_1, demultiplexer_2_out_2;
  wire [39:0] demultiplexer_3_out_0, demultiplexer_3_out_1, demultiplexer_3_out_2, multiplexer_1_out,
       undriven;
  wire [39:32] undriven_2;

  Comparator Is_I_Format (.a(INSN[12]), .b(1'b0), .eq(Is_I_Format_eq));  // open: gt, lt
  Counter counter_1 (.en(1'b1), .C(CLK), .clr(comparator_1_eq), .out(counter_1_out[0]));  // open: ovf
  not not_1 (not_1_out, Is_I_Format_eq);
  Comparator #(.Bits(2)) comparator_1 (.a(counter_1_out), .b(2'b11), .eq(comparator_1_eq));  // open: gt, lt
  Multiplexer #(.Bits(40)) multiplexer_1 (
    .sel(not_1_out), .in_0({undriven_2, INSN[7:0], 18'h20001, TagDst[4:0], 1'b1}), .in_1(undriven),
    .out(multiplexer_1_out));
  Demultiplexer #(.Selector_Bits(2)) demultiplexer_1 (
    .sel(counter_1_out), .out_0(demultiplexer_1_out_0), .out_1(demultiplexer_1_out_1),
    .out_2(demultiplexer_1_out_2));  // open: in, out_3
  Demultiplexer #(.Selector_Bits(2), .Bits(6)) demultiplexer_2 (
    .sel(counter_1_out), .out_0(demultiplexer_2_out_0), .out_1(demultiplexer_2_out_1),
    .out_2(demultiplexer_2_out_2));  // open: in, out_3
  Demultiplexer #(.Selector_Bits(2), .Bits(40)) demultiplexer_3 (
    .sel(counter_1_out), .in(multiplexer_1_out), .out_0(demultiplexer_3_out_0),
    .out_1(demultiplexer_3_out_1), .out_2(demultiplexer_3_out_2));  // open: out_3
  Demultiplexer #(.Selector_Bits(2)) demultiplexer_4 (
    .sel(counter_1_out), .in(CLK), .out_0(demultiplexer_4_out_0), .out_1(demultiplexer_4_out_1),
    .out_2(demultiplexer_4_out_2));  // open: out_3
  issue_queue_entry IQEntry0 (
    .CLK(demultiplexer_4_out_0), .V_IN(demultiplexer_3_out_0[0]), .TagDst_IN(demultiplexer_3_out_0[5:1]),
    .R1Rdy_IN(demultiplexer_3_out_0[6]), .R1TagVal_IN(demultiplexer_3_out_0[22:7]),
    .R2Rdy_IN(demultiplexer_3_out_0[23]), .R2TagVal_IN(demultiplexer_3_out_0[39:24]),
    .V_WE(demultiplexer_2_out_0[0]), .TagDst_WE(demultiplexer_2_out_0[1]),
    .R1Rdy_WE(demultiplexer_2_out_0[2]), .R1TagVal_WE(demultiplexer_2_out_0[3]),
    .R2Rdy_WE(demultiplexer_2_out_0[4]), .R2TagVal_WE(demultiplexer_2_out_0[5]), .CLR(demultiplexer_1_out_0));  // open: V_OUT, TagDst_OUT, R1Rdy_OUT, R1TagVal_OUT, R2Rdy_OUT, R2TagVal_OUT
  issue_queue_entry IQEntry1 (
    .CLK(demultiplexer_4_out_1), .V_IN(demultiplexer_3_out_1[0]), .TagDst_IN(demultiplexer_3_out_1[5:1]),
    .R1Rdy_IN(demultiplexer_3_out_1[6]), .R1TagVal_IN(demultiplexer_3_out_1[22:7]),
    .R2Rdy_IN(demultiplexer_3_out_1[23]), .R2TagVal_IN(demultiplexer_3_out_1[39:24]),
    .V_WE(demultiplexer_2_out_1[0]), .TagDst_WE(demultiplexer_2_out_1[1]),
    .R1Rdy_WE(demultiplexer_2_out_1[2]), .R1TagVal_WE(demultiplexer_2_out_1[3]),
    .R2Rdy_WE(demultiplexer_2_out_1[4]), .R2TagVal_WE(demultiplexer_2_out_1[5]), .CLR(demultiplexer_1_out_1));  // open: V_OUT, TagDst_OUT, R1Rdy_OUT, R1TagVal_OUT, R2Rdy_OUT, R2TagVal_OUT
  issue_queue_entry IQEntry2 (
    .CLK(demultiplexer_4_out_2), .V_IN(demultiplexer_3_out_2[0]), .TagDst_IN(demultiplexer_3_out_2[5:1]),
    .R1Rdy_IN(demultiplexer_3_out_2[6]), .R1TagVal_IN(demultiplexer_3_out_2[22:7]),
    .R2Rdy_IN(demultiplexer_3_out_2[23]), .R2TagVal_IN(demultiplexer_3_out_2[39:24]),
    .V_WE(demultiplexer_2_out_2[0]), .TagDst_WE(demultiplexer_2_out_2[1]),
    .R1Rdy_WE(demultiplexer_2_out_2[2]), .R1TagVal_WE(demultiplexer_2_out_2[3]),
    .R2Rdy_WE(demultiplexer_2_out_2[4]), .R2TagVal_WE(demultiplexer_2_out_2[5]), .CLR(demultiplexer_1_out_2));  // open: V_OUT, TagDst_OUT, R1Rdy_OUT, R1TagVal_OUT, R2Rdy_OUT, R2TagVal_OUT
  // Pins of 1 and 2 bits meet at counter_1_out
  // Pins of 1 and 4 bits meet at INSN[15:12]
  // Pins of 1 and 4 bits meet at 4'b0000
  // Pins of 5 and 16 bits meet at TagDst
  // Pins of 8 and 16 bits meet at {undriven_2, INSN[7:0]}

  // Notes on the sheet:
  //   Issue Queue (IQ)
  //   For I-Format insns, we can just 
  //   put the Imm8 as R2 and mark it,
  //   also using 0 for R1 with it marked
endmodule
