// Digital circuit issue_queue_entry.dig as structural Verilog
module issue_queue_entry (
  input  CLK,
  input  V_IN,
  input  [4:0] TagDst_IN,
  input  R1Rdy_IN,
  input  [15:0] R1TagVal_IN,
  input  R2Rdy_IN,
  input  [15:0] R2TagVal_IN,
  input  V_WE,
  input  TagDst_WE,
  input  R1Rdy_WE,
  input  R1TagVal_WE,
  input  R2Rdy_WE,
  input  R2TagVal_WE,
  input  CLR,
  output V_OUT,
  output [4:0] TagDst_OUT,
  output R1Rdy_OUT,
  output [15:0] R1TagVal_OUT,
  output R2Rdy_OUT,
  output [15:0] R2TagVal_OUT
);

  wire multiplexer_1_out, multiplexer_3_out, multiplexer_5_out, or_1_out, or_2_out, or_3_out, or_4_out,
       or_5_out, or_6_out;
  wire [4:0] multiplexer_2_out;
  wire [15:0] multiplexer_4_out, multiplexer_6_out;

  or or_1 (or_1_out, CLR, V_WE);
  or or_2 (or_2_out, TagDst_WE, CLR);
  or or_3 (or_3_out, R1Rdy_WE, CLR);
  or or_4 (or_4_out, R1TagVal_WE, CLR);
  or or_5 (or_5_out, R2Rdy_WE, CLR);
  or or_6 (or_6_out, R2TagVal_WE, CLR);
  Multiplexer multiplexer_1 (.sel(CLR), .in_0(V_IN), .in_1(1'b0), .out(multiplexer_1_out));
  Multiplexer #(.Bits(5)) multiplexer_2 (.sel(CLR), .in_0(TagDst_IN), .in_1({5{1'b0}}), .out(multiplexer_2_out));
  Multiplexer multiplexer_3 (.sel(CLR), .in_0(R1Rdy_IN), .in_1(1'b0), .out(multiplexer_3_out));
  Multiplexer #(.Bits(16)) multiplexer_4 (.sel(CLR), .in_0(R1TagVal_IN), .in_1({16{1'b0}}), .out(multiplexer_4_out));
  Multiplexer multiplexer_5 (.sel(CLR), .in_0(R2Rdy_IN), .in_1(1'b0), .out(multiplexer_5_out));
  Multiplexer #(.Bits(16)) multiplexer_6 (.sel(CLR), .in_0(R2TagVal_IN), .in_1({16{1'b0}}), .out(multiplexer_6_out));
  Register V (.D(multiplexer_1_out), .C(CLK), .en(or_1_out), .Q(V_OUT));
  Register #(.Bits(5)) TagDst (.D(multiplexer_2_out), .C(CLK), .en(or_2_out), .Q(TagDst_OUT));
  Register R1Rdy (.D(multiplexer_3_out), .C(CLK), .en(or_3_out), .Q(R1Rdy_OUT));
  Register #(.Bits(16)) R1TagVal (.D(multiplexer_4_out), .C(CLK), .en(or_4_out), .Q(R1TagVal_OUT));
  Register R2Rdy (.D(multiplexer_5_out), .C(CLK), .en(or_5_out), .Q(R2Rdy_OUT));
  Register #(.Bits(16)) R2TagVal (.D(multiplexer_6_out), .C(CLK), .en(or_6_out), .Q(R2TagVal_OUT));
endmodule
