// Digital circuit rename_map_table.dig as structural Verilog
module rename_map_table (
  input  [2:0] Register,
  input  CLK,
  input  [15:0] V_IN,
  input  [15:0] Tag_IN,
  output [15:0] V_OUT,
  output [15:0] Tag_OUT
);

  wire decoder_1_out_0, decoder_1_out_1, decoder_1_out_2, decoder_1_out_3, decoder_1_out_4, decoder_1_out_5,
       decoder_1_out_7;
  wire [15:0] demultiplexer_1_out_0, demultiplexer_1_out_1, demultiplexer_1_out_2, demultiplexer_1_out_3,
       demultiplexer_1_out_4, demultiplexer_1_out_5, demultiplexer_1_out_7, demultiplexer_2_out_0,
       demultiplexer_2_out_1, demultiplexer_2_out_2, demultiplexer_2_out_3, demultiplexer_2_out_4,
       demultiplexer_2_out_5, demultiplexer_2_out_7, R0_Tag_q, R0_V_q, R1_Tag_q, R1_V_q, R2_Tag_q, R2_V_q,
       R3_Tag_q, R3_V_q, R4_Tag_q, R4_V_q, R5_Tag_q, R5_V_q, R7_Tag_q, R7_V_q;

  Demultiplexer #(.Selector_Bits(3), .Bits(16)) demultiplexer_1 (
    .sel(V_IN[2:0]), .in(Tag_IN), .out_0(demultiplexer_1_out_0), .out_1(demultiplexer_1_out_1),
    .out_2(demultiplexer_1_out_2), .out_3(demultiplexer_1_out_3), .out_4(demultiplexer_1_out_4),
    .out_5(demultiplexer_1_out_5), .out_7(demultiplexer_1_out_7));  // open: out_6
  Demultiplexer #(.Selector_Bits(3), .Bits(16)) demultiplexer_2 (
    .sel(Register), .in(V_IN), .out_0(demultiplexer_2_out_0), .out_1(demultiplexer_2_out_1),
    .out_2(demultiplexer_2_out_2), .out_3(demultiplexer_2_out_3), .out_4(demultiplexer_2_out_4),
    .out_5(demultiplexer_2_out_5), .out_7(demultiplexer_2_out_7));  // open: out_6
  Decoder #(.Selector_Bits(3)) decoder_1 (
    .sel(Register), .out_0(decoder_1_out_0), .out_1(decoder_1_out_1), .out_2(decoder_1_out_2),
    .out_3(decoder_1_out_3), .out_4(decoder_1_out_4), .out_5(decoder_1_out_5), .out_7(decoder_1_out_7));  // open: out_6
  Register #(.Bits(16)) R0_V (.D(demultiplexer_2_out_0), .C(CLK), .en(decoder_1_out_0), .Q(R0_V_q));
  Register R0_Tag (.D(demultiplexer_1_out_0[0]), .C(CLK), .en(decoder_1_out_0), .Q(R0_Tag_q[0]));
  Register R1_V (.D(demultiplexer_2_out_1[0]), .C(CLK), .en(decoder_1_out_1), .Q(R1_V_q[0]));
  Register R1_Tag (.D(demultiplexer_1_out_1[0]), .C(CLK), .en(decoder_1_out_1), .Q(R1_Tag_q[0]));
  Register R2_V (.D(demultiplexer_2_out_2[0]), .C(CLK), .en(decoder_1_out_2), .Q(R2_V_q[0]));
  Register R2_Tag (.D(demultiplexer_1_out_2[0]), .C(CLK), .en(decoder_1_out_2), .Q(R2_Tag_q[0]));
  Register R3_V (.D(demultiplexer_2_out_3[0]), .C(CLK), .en(decoder_1_out_3), .Q(R3_V_q[0]));
  Register R3_Tag (.D(demultiplexer_1_out_3[0]), .C(CLK), .en(decoder_1_out_3), .Q(R3_Tag_q[0]));
  Register R4_V (.D(demultiplexer_2_out_4[0]), .C(CLK), .en(decoder_1_out_4), .Q(R4_V_q[0]));
  Register R4_Tag (.D(demultiplexer_1_out_4[0]), .C(CLK), .en(decoder_1_out_4), .Q(R4_Tag_q[0]));
  Register R5_V (.D(demultiplexer_2_out_5[0]), .C(CLK), .en(decoder_1_out_5), .Q(R5_V_q[0]));
  Register R5_Tag (.D(demultiplexer_1_out_5[0]), .C(CLK), .en(decoder_1_out_5), .Q(R5_Tag_q[0]));
  Register R7_V (.D(demultiplexer_2_out_7[0]), .C(CLK), .en(decoder_1_out_7), .Q(R7_V_q[0]));
  Register R7_Tag (.D(demultiplexer_1_out_7[0]), .C(CLK), .en(decoder_1_out_7), .Q(R7_Tag_q[0]));
  Multiplexer #(.Selector_Bits(3), .Bits(16)) multiplexer_1 (
    .sel(Register), .in_0(R0_V_q), .in_1(R1_V_q), .in_2(R2_V_q), .in_3(R3_V_q), .in_4(R4_V_q), .in_5(R5_V_q),
    .in_7(R7_V_q), .out(V_OUT));  // open: in_6
  Multiplexer #(.Selector_Bits(3), .Bits(16)) multiplexer_2 (
    .sel(Register), .in_0(R0_Tag_q), .in_1(R1_Tag_q), .in_2(R2_Tag_q), .in_3(R3_Tag_q), .in_4(R4_Tag_q),
    .in_5(R5_Tag_q), .in_7(R7_Tag_q), .out(Tag_OUT));  // open: in_6
  // Pins of 1 and 16 bits meet at demultiplexer_1_out_0
  // Pins of 1 and 16 bits meet at R0_Tag_q
  // Pins of 1 and 16 bits meet at demultiplexer_2_out_1
  // Pins of 1 and 16 bits meet at R1_V_q
  // Pins of 1 and 16 bits meet at demultiplexer_1_out_1
  // Pins of 1 and 16 bits meet at R1_Tag_q
  // Pins of 1 and 16 bits meet at demultiplexer_2_out_2
  // Pins of 1 and 16 bits meet at R2_V_q
  // Pins of 1 and 16 bits meet at demultiplexer_1_out_2
  // Pins of 1 and 16 bits meet at R2_Tag_q
  // Pins of 1 and 16 bits meet at demultiplexer_2_out_3
  // Pins of 1 and 16 bits meet at R3_V_q

  // Notes on the sheet:
  //   Rename Map Table (RMT)
endmodule
